# Fritzing sketch pad (saved by Fritzing 0.9.3b)

parts:
  Part1 = Arduino Micro (Rev3)
  U1 = SLIDER [package=slider]
  U2 = SLIDER [package=slider]
  U3 = SLIDER [package=slider]
  Generic_4x4_button_keypad1 = Generic 4x4 Keypad
  S1 = Taiway 100-SP-X-T1 SPDT Miniature Toggle Switch [part_number=100-SP-X-T1-0-0-B1-M2 package=THT]
  S2 = Taiway 100-SP-X-T1 SPDT Miniature Toggle Switch [part_number=100-SP-X-T1-0-0-B1-M2 package=THT]
  S3 = Taiway 100-SP-X-T1 SPDT Miniature Toggle Switch [part_number=100-SP-X-T1-0-0-B1-M2 package=THT]
  SW1 = ENCODER_RGB_CA [package=encoder_led_3]
  SW2 = ENCODER_RGB_CA [package=encoder_led_3]  # not connected
  SW3 = ENCODER_RGB_CA [package=encoder_led_3]  # not connected
  SW4 = ENCODER_RGB_CA [package=encoder_led_3]
  U4 = 74HC165 [part_number=SN74LS165 package="DIP16 [THT]"]  # not connected

nets:
  N1: Part1.GND, U1.E, U2.E, U3.E, S1.COM, S2.COM, S3.COM, SW4.C
  N2: Part1.D2/SDA, S3.L2
  N3: Part1.D3/SCL, S2.L2
  N4: Part1.D4_PWM/A6, S1.L2
  N5: Part1.D5_PWM, Generic_4x4_button_keypad1.R4
  N6: Part1.D6_PWM/A7, Generic_4x4_button_keypad1.R3
  N7: Part1.D7, Generic_4x4_button_keypad1.R2
  N8: Part1.D8_PWM/A8, Generic_4x4_button_keypad1.R1
  N9: Part1.D9_PWM/A9, Generic_4x4_button_keypad1.C1
  N10: Part1.D10_PWM/A10, Generic_4x4_button_keypad1.C2
  N11: Part1.D11_PWM, Generic_4x4_button_keypad1.C3
  N12: Part1.D12_PWM/A11, Generic_4x4_button_keypad1.C4
  N13: Part1.5V, U1.A, U2.A, U3.A, SW1.B
  N14: Part1.A2, U3.S
  N15: Part1.A1, U2.S
  N16: Part1.A0, U1.S

notes:
  74HC165

custom parts:
  Generic 4x4 Keypad: generic 4x4 keypad 4 rows of four 6 mm tact switches cheap and nasty but works
  74HC165: 8-bit parallel-load shift registers
